# Fritzing sketch fritzing (saved by Fritzing 0.9.2b)
breadboards: 1

parts:
  Part1 = Photon
  U1 = MLX90614 [package=to-39]
  U2 = GAS_SENSOR [package=mq-3]
  RHT1 = Humidity and Temperature Sensor RHT03
  R1 = Resistor [tolerance=±5% resistance=100 package="2010 [SMD]"]
  R2 = PHOTOCELL [package=photocell-kit]
  R3 = Resistor [tolerance=±5% resistance=100 package="2010 [SMD]"]

nets:
  N1: Part1.A5, R2.P$1, R3.Pin_1
  N2: Part1.GND, U2.B1, R3.Pin_0
  N3: Part1.D0, U1.SCL_VZ
  N4: Part1.D2, RHT1.GND_1
  3V3: Part1.3V3, U1.PWM_SDA, RHT1.Vcc, RHT1.GND_2, R1.Pin_0, R2.P$2
  N5: RHT1.Data-signal, R1.Pin_1

notes:
  MQ-7
  vcc, gnd, do, ao
  PIR
  gnd, data, vcc
